// Logisim project Full Adder.circ as structural Verilog: 8 circuits, main circuit Main Arithmatic Unit (Mag.)
module Main (
  input  in_1,
  input  in_2,
  input  in_3,
  input  in_4,
  input  in_5,
  input  in_6,
  input  in_7,
  input  in_8,
  output out_9,
  output out_10,
  output out_11,
  output out_12,
  output out_13,
  output out_14,
  output out_15,
  output out_16,
  output out_17
);

  Main_Arithmatic_Unit__Mag main_arithmatic_unit_mag_1 (
    .S0(in_7), .S1(in_8), .B2(in_1), .B1(in_2), .B0(in_3), .A2(in_4), .A1(in_5), .A0(in_6), .X0_2(out_17),
    .X1_2(out_16), .X2(out_12), .X1(out_13), .X0(out_14), .X3(out_11), .Sign(out_10), .Sign_2(out_15),
    .E_F(out_9));
endmodule

module Main_Arithmatic_Unit__Mag (
  input  B2,
  input  B1,
  input  B0,
  input  A2,
  input  A1,
  input  A0,
  input  S0,
  input  S1,
  output Sign,
  output X3,
  output X2,
  output X1,
  output X0,
  output E_F,
  output Sign_2,
  output X1_2,
  output X0_2
);

  Multiplieng_Unit multiplieng_unit_1 (
    .B2(B2), .A2(A2), .B1(B1), .B0(B0), .A1(A1), .A0(A0), .N_Enable(S1), .X2(X2), .X1(X1), .X0(X0),
    .Sign(Sign), .X3(X3));
  Add_Sub_Unit add_sub_unit_1 (
    .B2(B2), .B1(B1), .B0(B0), .A2(A2), .A1(A1), .A0(A0), .S1(S1), .S0(S0), .E_F(E_F), .Sign(Sign_2),
    .X1(X1_2), .X0(X0_2));
endmodule

module Add_Sub_Unit (
  input  B2,
  input  B1,
  input  B0,
  input  A2,
  input  A1,
  input  A0,
  input  S0,
  input  S1,
  output Sign,
  output X1,
  output X0,
  output E_F
);

  wire and_1_out, n3_bit_inverter_in_1_x0_2, n3_bit_inverter_in_1_x1_2, n3_bit_inverter_in_1_x2_2,
       n3_bit_inverter_in_2_x0_2, n3_bit_inverter_in_2_x1_2, n3_bit_inverter_in_2_x2_2, n4_bit_adder_1_cout,
       n4_bit_adder_1_s1, n4_bit_adder_1_s2, n4_bit_adder_1_s3, xnor_1_out, xor_1_out, xor_2_out, xor_3_out;

  xor xor_1 (xor_1_out, n3_bit_inverter_in_1_x2_2, S0);
  xnor xnor_1 (xnor_1_out, xor_1_out, n3_bit_inverter_in_2_x2_2);
  _3_Bit_Inverter_in u_3_bit_inverter_in_1 (
    .X2(B2), .X1(B1), .X0(B0), .X2_2(n3_bit_inverter_in_1_x2_2), .X1_2(n3_bit_inverter_in_1_x1_2),
    .X0_2(n3_bit_inverter_in_1_x0_2));
  xor xor_2 (xor_2_out, n3_bit_inverter_in_1_x1_2, S0);
  _4_Bit_Adder u_4_bit_adder_1 (
    .A0(S0), .A1(n3_bit_inverter_in_2_x0_2), .A2(n3_bit_inverter_in_2_x1_2), .B0(S0), .B1(xor_3_out),
    .B2(xor_2_out), .S1(n4_bit_adder_1_s1), .S2(n4_bit_adder_1_s2), .Cout(n4_bit_adder_1_cout),
    .S3(n4_bit_adder_1_s3), .B2_2(xor_1_out), .A3(n3_bit_inverter_in_2_x2_2), .Cin(1'b0), .Enable(S1));  // open: S0
  and and_1 (and_1_out, xnor_1_out, n4_bit_adder_1_s3);
  or or_1 (E_F, and_1_out, n4_bit_adder_1_cout);
  xor xor_3 (xor_3_out, n3_bit_inverter_in_1_x0_2, S0);
  _3_Bit_Inverter_out u_3_bit_inverter_out_1 (
    .X2(n4_bit_adder_1_s3), .X1(n4_bit_adder_1_s2), .X0(n4_bit_adder_1_s1), .X2_2(Sign), .X1_2(X1), .X0_2(X0));
  _3_Bit_Inverter_in u_3_bit_inverter_in_2 (
    .X2(A2), .X1(A1), .X0(A0), .X2_2(n3_bit_inverter_in_2_x2_2), .X1_2(n3_bit_inverter_in_2_x1_2),
    .X0_2(n3_bit_inverter_in_2_x0_2));
endmodule

module Multiplieng_Unit (
  input  B2,
  input  A2,
  input  B1,
  input  B0,
  input  A1,
  input  A0,
  input  N_Enable,
  output Sign,
  output X3,
  output X2,
  output X1,
  output X0
);

  wire and_1_out, and_2_out, and_3_out, and_4_out, and_5_out, xor_1_out;

  and and_1 (and_1_out, A2, xor_1_out);
  and and_2 (and_2_out, B2, xor_1_out);
  _4_Bit_Adder u_4_bit_adder_1 (
    .A0(and_5_out), .A1(1'b0), .A2(1'b0), .B0(and_4_out), .B1(and_3_out), .B2(1'b0), .S0(X1), .S1(X2),
    .S2(X3), .S3(Sign), .B2_2(and_2_out), .A3(and_1_out), .Cin(1'b0), .Enable(xor_1_out));  // open: Cout
  and and_3 (and_3_out, B1, xor_1_out, A1);
  and and_4 (and_4_out, B0, xor_1_out, A1);
  and and_5 (and_5_out, B1, xor_1_out, A0);
  and and_6 (X0, B0, xor_1_out, A0);
  xor xor_1 (xor_1_out, N_Enable, 1'b1);

  // Notes on the sheet:
  //   signs
  //   A1B0
  //   A1B1
  //   A0B1
  //   A0B0
endmodule

module _3_Bit_Inverter_in (
  input  X2,
  input  X1,
  input  X0,
  output X2_2,
  output X1_2,
  output X0_2
);

  wire and_1_out, nor_1_out, nor_2_out, or_1_out, xor_2_out;

  and and_1 (and_1_out, X2, X0);
  nor nor_1 (nor_1_out, X1, X0);
  or or_1 (or_1_out, X1, X0);
  xor xor_1 (X1_2, and_1_out, X1);
  xor xor_2 (xor_2_out, X2, nor_1_out);
  nor nor_2 (nor_2_out, or_1_out, X2);
  xor xor_3 (X2_2, xor_2_out, nor_2_out);

  assign X0_2 = X0;
endmodule

module _3_Bit_Inverter_out (
  input  X2,
  input  X1,
  input  X0,
  output X2_2,
  output X1_2,
  output X0_2
);

  wire and_1_out;

  and and_1 (and_1_out, X2, X0);
  xor xor_1 (X1_2, and_1_out, X1);

  assign X0_2 = X0;
  assign X2_2 = X2;
endmodule

module _4_Bit_Adder (
  input  Cin,
  input  Enable,
  input  A0,
  input  A1,
  input  A2,
  input  A3,
  input  B0,
  input  B1,
  input  B2,
  input  B2_2,
  output S0,
  output S1,
  output S2,
  output S3,
  output Cout
);

  wire F_A_2_carry_2, F_A_2_sum, F_A_3_carry_2, F_A_3_sum, F_A_4_carry_2, F_A_4_sum, F_A_carry_2, F_A_sum;

  Full_Adder F_A (.Carry(Cin), .X(A0), .Y(B0), .Sum(F_A_sum), .Carry_2(F_A_carry_2));
  Full_Adder F_A_2 (.Carry(F_A_carry_2), .X(A1), .Y(B1), .Sum(F_A_2_sum), .Carry_2(F_A_2_carry_2));
  Full_Adder F_A_3 (.Carry(F_A_2_carry_2), .X(A2), .Y(B2), .Sum(F_A_3_sum), .Carry_2(F_A_3_carry_2));
  Full_Adder F_A_4 (.Carry(F_A_3_carry_2), .X(A3), .Y(B2_2), .Sum(F_A_4_sum), .Carry_2(F_A_4_carry_2));
  and and_1 (S0, F_A_sum, Enable);
  and and_2 (S1, F_A_2_sum, Enable);
  and and_3 (S2, F_A_3_sum, Enable);
  and and_4 (S3, F_A_4_sum, Enable);
  and and_5 (Cout, F_A_4_carry_2, Enable);
endmodule

module Full_Adder (
  input  Carry,
  input  X,
  input  Y,
  output Sum,
  output Carry_2
);

  wire and_1_out, and_2_out, xor_1_out;

  xor xor_1 (xor_1_out, X, Y);
  and and_1 (and_1_out, X, Y);
  xor xor_2 (Sum, xor_1_out, Carry);
  and and_2 (and_2_out, xor_1_out, Carry);
  or or_1 (Carry_2, and_2_out, and_1_out);
endmodule
